# Fritzing sketch 20LEDBarGraph (saved by Fritzing 0.9.2b)
breadboards: 1

parts:
  Placa_Nano = Arduino Nano (Rev3.0)
  LED1 = LED - 5mm [color="Red (633nm)" package="5 mm [THT]"]
  LED2 = LED - 5mm [color="Red (633nm)" package="5 mm [THT]"]
  LED4 = LED - 5mm [color="Red (633nm)" package="5 mm [THT]"]
  LED5 = LED - 5mm [color="Red (633nm)" package="5 mm [THT]"]
  LED6 = LED - 5mm [color="Red (633nm)" package="5 mm [THT]"]
  LED7 = LED - 5mm [color="Red (633nm)" package="5 mm [THT]"]
  LED8 = LED - 5mm [color="Red (633nm)" package="5 mm [THT]"]
  LED9 = LED - 5mm [color="Red (633nm)" package="5 mm [THT]"]
  LED10 = LED - 5mm [color="Red (633nm)" package="5 mm [THT]"]
  J1 = Piezo Speaker
  U1 = POT [package=3362u]
  S1 = Momentary Switch [package=ksa_sealed_tac_switch]
  R1 = Resistor [tolerance=±5% resistance=220 package="2010 [SMD]"]
  LED11 = LED - 5mm [color="Blue (430nm)" package="5 mm [THT]"]
  R2 = Resistor [tolerance=±5% resistance=220 package="2010 [SMD]"]
  LED3 = LED - 5mm [color="Red (633nm)" package="5 mm [THT]"]

nets:
  N1: Placa_Nano.GND, J1.pin1, U1.E, S1.3, S1.4, R1.Pin_1, R2.Pin_1
  N2: Placa_Nano.D2, LED1.anode
  N3: Placa_Nano.D3, LED2.anode
  N4: Placa_Nano.D4, LED3.anode
  N5: Placa_Nano.D5, LED4.anode
  N6: Placa_Nano.D6, LED5.anode
  N7: Placa_Nano.D7, LED6.anode
  N8: Placa_Nano.D8, LED7.anode
  N9: Placa_Nano.D9, LED8.anode
  N10: Placa_Nano.D10, LED9.anode
  N11: Placa_Nano.D11/MOSI, LED10.anode
  N12: Placa_Nano.D12/MISO, J1.pin2
  N13: Placa_Nano.5V, U1.A
  N14: Placa_Nano.A2, U1.S
  N15: Placa_Nano.A1, S1.1, S1.2
  N16: Placa_Nano.D13/SCK, LED11.anode
  N17: LED1.cathode, LED2.cathode, LED4.cathode, LED5.cathode, LED6.cathode, LED7.cathode, LED8.cathode, LED9.cathode, LED10.cathode, R1.Pin_0, LED3.cathode
  N18: LED11.cathode, R2.Pin_0
